// Logisim project ALU.circ as structural Verilog: 1 circuit, main circuit main
module main (
  input  [4:0] in_1,
  input  [15:0] in_2,
  input  [15:0] in_3,
  input  [3:0] in_4,
  output [15:0] out_5,
  output out_6,
  output out_7
);

  wire [15:0] main_1_out_4, main_2_p4, main_3_out_4;

  Arithmatic_Unit_main main_1 (
    .in_1(in_1[2:0]), .in_2(in_2), .in_3(in_3), .out_4(main_1_out_4), .out_5(out_7), .out_6(out_6));
  // Logical_unit_0_2_main main_2: pin names not known; wires that end beside it: in_2, in_3, in_1[2:0], main_2_p4
  shifter_main main_3 (.in_1(in_1[2:0]), .in_2(in_2), .in_3(in_4), .out_4(main_3_out_4));
  Multiplexer #(.select(2), .width(16), .enable("false")) multiplexer_1 (
    .in0(main_1_out_4), .in1(main_2_p4), .in2(main_3_out_4), .out(out_5), .sel(in_1[4:3]));  // open: in3

  // Other names for the same wires on the sheet: operation[2:0] = in_1[2:0]; selector[1:0] = in_1[4:3];
  //   input_1[15:0] = in_2; input_2[15:0] = in_3; output[15:0] = out_5; over_flow = out_7; shift_amount[3:0] = in_4;
  //   zero = out_6
endmodule
