// Logisim project Control Unit.circ as structural Verilog: 4 circuits, main circuit main
module main (
  input  [15:0] in_1
);


  // Other names for the same wires on the sheet: Instruction[15:0] = in_1
endmodule

module ALU_Signal_generator (
  input  [6:0] in_1,
  output [3:0] out_2
);

  wire and_1_out, and_2_out, and_3_out, and_4_out, and_5_out, and_6_out, and_7_out, and_8_out, and_9_out,
       and_10_out, and_11_out, and_12_out, and_13_out, and_14_out, and_15_out, and_16_out, not_1_out,
       not_2_out, not_3_out, not_4_out, not_5_out, not_6_out, not_7_out, not_8_out, not_9_out, not_10_out,
       not_11_out, not_12_out, not_13_out, not_14_out, not_15_out, not_16_out, not_17_out, not_18_out,
       not_19_out, not_20_out, not_21_out, not_22_out, not_23_out, not_24_out, not_25_out, not_26_out,
       not_27_out, not_28_out, not_29_out, not_30_out, not_31_out;

  not not_1 (not_1_out, in_1[4]);
  not not_2 (not_2_out, in_1[6]);
  not not_3 (not_3_out, in_1[5]);
  not not_4 (not_4_out, in_1[3]);
  not not_5 (not_5_out, in_1[2]);
  not not_6 (not_6_out, in_1[5]);
  not not_7 (not_7_out, in_1[3]);
  not not_8 (not_8_out, in_1[5]);
  not not_9 (not_9_out, in_1[2]);
  not not_10 (not_10_out, in_1[5]);
  not not_11 (not_11_out, in_1[4]);
  not not_12 (not_12_out, in_1[3]);
  not not_13 (not_13_out, in_1[5]);
  not not_14 (not_14_out, in_1[2]);
  not not_15 (not_15_out, in_1[4]);
  not not_16 (not_16_out, in_1[3]);
  not not_17 (not_17_out, in_1[6]);
  not not_18 (not_18_out, in_1[5]);
  not not_19 (not_19_out, in_1[4]);
  not not_20 (not_20_out, in_1[1]);
  not not_21 (not_21_out, in_1[6]);
  not not_22 (not_22_out, in_1[5]);
  not not_23 (not_23_out, in_1[4]);
  not not_24 (not_24_out, in_1[2]);
  not not_25 (not_25_out, in_1[0]);
  not not_26 (not_26_out, in_1[6]);
  not not_27 (not_27_out, in_1[4]);
  not not_28 (not_28_out, in_1[5]);
  not not_29 (not_29_out, in_1[3]);
  not not_30 (not_30_out, in_1[2]);
  not not_31 (not_31_out, in_1[4]);
  and and_1 (and_1_out, in_1[5], not_1_out);
  and and_2 (and_2_out, in_1[6], in_1[3]);
  and and_3 (and_3_out, not_2_out, not_3_out, not_4_out, not_5_out);
  and and_4 (and_4_out, not_6_out, in_1[4], not_7_out);
  and and_5 (and_5_out, not_8_out, in_1[4], not_9_out);
  and and_6 (and_6_out, not_10_out, not_11_out, not_12_out, in_1[1]);
  and and_7 (and_7_out, not_13_out, in_1[4], in_1[3], not_14_out);
  and and_8 (and_8_out, in_1[5], not_15_out, in_1[3]);
  and and_9 (and_9_out, in_1[6], not_16_out);
  and and_10 (and_10_out, not_17_out, not_18_out, not_19_out, not_20_out, in_1[0]);
  and and_11 (and_11_out, not_21_out, not_22_out, not_23_out, not_24_out, in_1[1], not_25_out);
  and and_12 (and_12_out, not_26_out, not_27_out, in_1[2], in_1[0]);
  and and_13 (and_13_out, not_28_out, in_1[4], not_29_out, in_1[2]);
  and and_14 (and_14_out, in_1[4], in_1[3], not_30_out);
  and and_15 (and_15_out, in_1[5], not_31_out, in_1[2]);
  and and_16 (and_16_out, in_1[5], in_1[3], in_1[2]);
  or or_1 (out_2[3], and_1_out, and_2_out);
  or or_2 (out_2[2], and_3_out, and_4_out, and_5_out);
  or or_3 (out_2[1], and_6_out, and_7_out, and_8_out, and_9_out);
  or or_4 (out_2[0], and_10_out, and_11_out, and_12_out, and_13_out, and_14_out, and_15_out, and_16_out);

  // Other names for the same wires on the sheet: ALU_Op[3:0] = out_2; Func_Code[1:0] = in_1[1:0];
  //   Op_code[4:0] = in_1[6:2]
endmodule

module PC_Signal_Genorator (
  input  [4:0] in_1,
  output [3:0] out_2
);

  wire and_1_out, and_2_out, and_3_out, and_4_out, and_5_out, not_2_out, not_3_out, not_4_out, not_5_out,
       not_6_out, not_7_out;

  not not_1 (out_2[3], in_1[3]);
  not not_2 (not_2_out, in_1[1]);
  not not_3 (not_3_out, in_1[4]);
  not not_4 (not_4_out, in_1[3]);
  not not_5 (not_5_out, in_1[2]);
  not not_6 (not_6_out, in_1[4]);
  not not_7 (not_7_out, in_1[1]);
  and and_1 (and_1_out, in_1[3], in_1[2], in_1[1]);
  and and_2 (and_2_out, in_1[4], not_2_out);
  and and_3 (and_3_out, not_3_out, not_4_out, not_5_out, in_1[1]);
  and and_4 (and_4_out, not_6_out, in_1[3], in_1[2], in_1[1]);
  and and_5 (and_5_out, in_1[4], not_7_out);
  or or_1 (out_2[1], and_1_out, and_2_out);
  or or_2 (out_2[0], and_3_out, and_4_out, and_5_out);

  assign out_2[2] = in_1[0];

  // Other names for the same wires on the sheet: Op_Code[4:0] = in_1;
  //   PC_Signal[3:0] = {out_2[3], in_1[0], out_2[1:0]}
endmodule

module Mem_Reg_Signal_Generator (
  input  Op_Code___4,
  input  Op_Code___3,
  input  Op_Code___2,
  input  Op_Code___1,
  input  Op_Code___0,
  output out_6,
  output out_7,
  output out_8,
  output out_9
);
endmodule
