// Logisim project Full Circuit.circ as structural Verilog: 1 circuit, main circuit Full Circuit
module Full_Circuit (
);

  wire ALUsrc_Ex, ALUsrc_Id, CLK, Ext_Control_Ex, Ext_Control_Id, MemRead, MemRead_Ex, MemRead_Id, MemWrite,
       MemWrite_Ex, MemWrite_Id, multiplexer_3_out, multiplexer_4_out, not_1_out, not_2_out, not_3_out,
       Overflow, RegWrirte_Ex, RegWrite_Id, stall, zero;
  wire [1:0] F_Id, F_If, MemToReg_Ex, MemToReg_Id, RegDst_Id;
  wire [2:0] multiplexer_1_out, Rd_Ex, Rd_Id, Rd_If, Rs_Ex, Rs_Id, Rs_If, Rt_Ex, Rt_Id, Rt_If;
  wire [3:0] ALUop_Ex, ALUop_Id, PCsrc_Id, Shift_Amount_Ex, Shift_Amount_Id, Shift_Amount_If;
  wire [4:0] Imm_5_Id, Imm_5_If, OP_Id, OP_If;
  wire [10:0] Imm_11_Id, Imm_11_If;
  wire [15:0] ALU_out, bit_extender_1_out, Ext_Out_Ex, Ext_Out_Id, Imm_11__5, Imm_11__5_Ex, Imm_11__5_Id,
       ins, ins_Id, ins_If, Mem_out, multiplexer_2_out, multiplexer_5_out, Next_PC, Pc, PC_1, PC_Id, PC_If,
       Pc_If_t, R1, R2, R3, R4, R5, R6, R7, Rs_Data_Ex, Rs_Data_Id, Rt_Data, Rt_Data_Ex, Rt_Data_Id;

  not not_1 (not_1_out, stall);
  Register #(.width(16)) u_PC (.D(Next_PC), .en(not_1_out), .Q(Pc_If_t), .clk(CLK));  // open: clr
  InstructionMemory_main main_1 (
    .PC_Address(Pc_If_t), .out_2(Rt_If), .out_3(Rs_If), .out_5(Rd_If), .out_6(F_If), .out_7(OP_If),
    .out_8(Imm_5_If), .out_10(Imm_11_If), .out_9(Shift_Amount_If), .out_4(ins_If));
  Clock clock_1 (.out(CLK));
  // Probe on R1
  // Probe on Pc
  // Probe on R2
  // Probe on ins
  // Probe on R3
  // Probe on R4
  // Probe on R5
  // Probe on R6
  // Probe on R7
  // Reg_If_Id reg_if_id_1: pin names not known; wires that end beside it: PC_If, ins_If, Rt_If, Rs_If, Rd_If, F_If, OP_If, Imm_5_If, Shift_Amount_If, Imm_11_If, CLK, PC_Id, ins_Id, Rt_Id, Rs_Id, Rd_Id, F_Id, OP_Id, Imm_5_Id, Shift_Amount_Id, Imm_11_Id
  Control_Unit control_unit_1 (
    .in_1(OP_Id), .in_2(F_Id), .out_4(ALUsrc_Id), .out_3(ALUop_Id), .out_5(MemRead_Id), .out_6(MemWrite_Id),
    .out_7(Ext_Control_Id), .out_8(MemToReg_Id), .out_9(RegWrite_Id), .out_10(RegDst_Id), .out_11(PCsrc_Id));
  Multiplexer #(.select(2), .width(3), .enable("false")) multiplexer_1 (
    .in0(Rt_Id), .in1(Rd_Id), .in2(3'b001), .in3(3'b111), .out(multiplexer_1_out), .sel(RegDst_Id));
  Multiplexer #(.select(2), .width(16), .enable("false")) multiplexer_2 (
    .in0(ALU_out), .in1(Mem_out), .in2(Imm_11__5), .in3(PC_1), .out(multiplexer_2_out), .sel(MemToReg_Id));
  Hazard_Detection_Unit hazard_detection_unit_1 (
    .in_1(Rs_Id), .in_2(Rt_Id), .in_3(Rt_Ex), .in_4(MemRead_Ex), .out_5(stall));
  RegFile regfile_1 (
    .out_7(Rs_Data_Id), .in_2(Rs_Id), .in_6(CLK), .out_8(Rt_Data_Id), .in_3(Rt_Id), .in_5(RegWrite_Id),
    .in_4(multiplexer_1_out), .in_1(multiplexer_2_out), .out_9(R1), .out_10(R2), .out_11(R3), .out_12(R4),
    .out_13(R5), .out_14(R6), .out_15(R7));
  assign bit_extender_1_out = {{5{1'b0}}, Imm_11_Id};  // Bit_Extender bit_extender_1
  Extender extender_1 (.in_1(Ext_Control_Id), .in_2(Imm_5_Id), .out_3(Ext_Out_Id));
  Shifter #(.width(16)) shifter_1 (.in(bit_extender_1_out), .\dist (4'b0101), .out(Imm_11__5_Id));
  PC_control pc_control_1 (
    .in_1(PC_Id), .in_2(PCsrc_Id), .in_5(Imm_11_Id), .in_6(Imm_5_Id), .out_7(Next_PC), .in_3(Rs_Data_Id),
    .in_4(Rs_Data_Id));  // open: out_8
  Multiplexer #(.enable("false")) multiplexer_3 (
    .in0(RegWrite_Id), .in1(1'b0), .out(multiplexer_3_out), .sel(not_2_out));
  not not_2 (not_2_out, stall);
  Multiplexer #(.enable("false")) multiplexer_4 (
    .in0(MemWrite_Id), .in1(1'b0), .out(multiplexer_4_out), .sel(not_3_out));
  not not_3 (not_3_out, stall);
  Reg_Id_Ex reg_id_ex_1 (
    .in_3(ALUop_Id), .in_4(ALUsrc_Id), .in_5(MemRead_Id), .in_6(multiplexer_4_out), .in_7(Ext_Control_Id),
    .in_8(MemToReg_Id), .in_9(Rs_Data_Id), .in_10(Rt_Data_Id), .out_19(ALUop_Ex), .out_20(ALUsrc_Ex),
    .out_21(MemRead_Ex), .out_22(MemWrite_Ex), .out_23(Ext_Control_Ex), .out_24(MemToReg_Ex),
    .out_25(Rs_Data_Ex), .out_26(Rt_Data_Ex), .in_1(CLK), .in_15(Rs_Id), .out_31(Rs_Ex), .in_16(Rt_Id),
    .out_32(Rt_Ex), .in_17(Rd_Id), .out_33(Rd_Ex), .in_14(multiplexer_3_out), .out_30(RegWrirte_Ex),
    .in_12(Ext_Out_Id), .out_28(Ext_Out_Ex), .in_11(Shift_Amount_Id), .out_27(Shift_Amount_Ex),
    .in_13(Imm_11__5_Id), .out_29(Imm_11__5_Ex));  // open: in_2, out_18
  Multiplexer #(.width(16), .enable("false")) multiplexer_5 (
    .in0(Rt_Data_Ex), .in1(Ext_Out_Ex), .out(multiplexer_5_out), .sel(ALUsrc_Ex));
  // Forwarding_Unit forwarding_unit_1: pin names not known
  ALU alu_1 (
    .in_1(ALUop_Ex), .in_2(Rs_Data_Ex), .in_3(multiplexer_5_out), .in_4(Shift_Amount_Ex), .out_5(ALU_out),
    .out_6(zero), .out_7(Overflow));
  Data_Memory data_memory_1 (
    .Address(ALU_out), .Data_In(Rt_Data), .MemWrite(MemWrite), .MemRead(MemRead), .CLK(CLK),
    .Data_Out(Mem_out));
endmodule
