// Logisim project SingleCycleRISCmips.circ as structural Verilog: 1 circuit, main circuit main
module main (
);

  wire ALUsrc, CLK, MemRead, MemWrite, RegWrite, zero;
  wire [1:0] F, MemToReg, RegDst;
  wire [2:0] multiplexer_1_out, Rd, Rs, Rt;
  wire [3:0] ALUop, PCsrc, Shift_amount;
  wire [4:0] Imm_5, OP;
  wire [10:0] Imm_11;
  wire [15:0] ALU_out, bit_extender_1_out, Ext_Out, Imm_11__5, Mem_out, multiplexer_3_out, PC_1, PC_Address,
       regfile_1_p6, Rs_Data, Rt_Data;

  // PC pc_1: pin names not known; wires that end beside it: Imm_5, Imm_11, ALU_out, zero, PCsrc, PC_Address, PC_1
  InstructionMemory_main main_1 (
    .PC_Address(PC_Address), .out_2(Rt), .out_3(Rs), .out_4(Rd), .out_5(F), .out_6(OP), .out_7(Imm_5),
    .out_9(Imm_11), .out_8(Shift_amount));
  Multiplexer #(.select(2), .width(3), .enable("false")) multiplexer_1 (
    .in0(Rt), .in1(Rd), .in2(3'b001), .in3(3'b111), .out(multiplexer_1_out), .sel(RegDst));
  // RegFile regfile_1: pin names not known; wires that end beside it: Rs, Rt, multiplexer_1_out, CLK, RegWrite, regfile_1_p6
  Multiplexer #(.select(2), .width(16), .enable("false")) multiplexer_2 (
    .in0(ALU_out), .in1(Mem_out), .in2(Imm_11__5), .in3(PC_1), .out(regfile_1_p6), .sel(MemToReg));
  Multiplexer #(.width(16), .enable("false")) multiplexer_3 (
    .in0(Rt_Data), .in1(Ext_Out), .out(multiplexer_3_out), .sel(ALUsrc));
  assign bit_extender_1_out = {{5{1'b0}}, Imm_11};  // Bit_Extender bit_extender_1
  // ALU alu_1: pin names not known; wires that end beside it: ALUsrc, Rs_Data, multiplexer_3_out, Shift_amount, ALUop
  // Extender_main main_2: pin names not known; wires that end beside it: Imm_5
  Shifter #(.width(16)) shifter_1 (.in(bit_extender_1_out), .\dist (4'b0101), .out(Imm_11__5));
  // Data_Memory data_memory_1: pin names not known; wires that end beside it: ALU_out, Rt_Data, CLK, MemRead, MemWrite, Mem_out
endmodule
